// Logisim project 减法器.circ as structural Verilog: 3 circuits, main circuit 4位原码减法器
module \_4位原码减法器  (
  input  in_1,
  input  [3:0] in_2,
  input  in_3,
  input  [3:0] in_4,
  output out_5,
  output [3:0] out_6
);

  wire adder_1_cout, adder_1_out, adder_2_cout, adder_2_out, adder_3_cout, adder_3_out, adder_4_out,
       and_1_out, and_2_out, and_3_out, comparator_1_gt, comparator_1_lt, multiplexer_1_out,
       multiplexer_2_out, multiplexer_3_out, multiplexer_4_out, multiplexer_5_out, multiplexer_6_out,
       multiplexer_7_out, multiplexer_8_out, not_1_out, not_2_out, not_3_out, not_4_out, subtractor_1_bout,
       subtractor_1_out, subtractor_2_bout, subtractor_2_out, subtractor_3_bout, subtractor_3_out,
       subtractor_4_out, xor_1_out;
  wire [3:0] and_4_out, and_8_out;

  Hex_Digit_Display hex_digit_display_1 (.value(in_2));  // open: dp
  Hex_Digit_Display hex_digit_display_2 (.value(in_4));  // open: dp
  not not_1 (not_1_out, in_3);
  Comparator #(.width(4)) comparator_1 (.a(in_2), .b(in_4), .gt(comparator_1_gt), .lt(comparator_1_lt));  // open: eq
  not not_2 (not_2_out, in_3);
  not not_3 (not_3_out, in_1);
  Adder #(.width(1)) adder_1 (.a(in_2[0]), .b(in_4[0]), .out(adder_1_out), .cin(1'b0), .cout(adder_1_cout));
  Adder #(.width(1)) adder_2 (.a(in_2[1]), .b(in_4[1]), .out(adder_2_out), .cin(adder_1_cout), .cout(adder_2_cout));
  Adder #(.width(1)) adder_3 (.a(in_2[2]), .b(in_4[2]), .out(adder_3_out), .cin(adder_2_cout), .cout(adder_3_cout));
  Adder #(.width(1)) adder_4 (.a(in_2[3]), .b(in_4[3]), .out(adder_4_out), .cin(adder_3_cout));  // open: cout
  Multiplexer #(.enable("false")) multiplexer_1 (
    .in0(in_2[0]), .in1(in_4[0]), .out(multiplexer_1_out), .sel(comparator_1_lt));
  Multiplexer #(.enable("false")) multiplexer_2 (
    .in0(in_4[0]), .in1(in_2[0]), .out(multiplexer_2_out), .sel(comparator_1_lt));
  Multiplexer #(.enable("false")) multiplexer_3 (
    .in0(in_2[1]), .in1(in_4[1]), .out(multiplexer_3_out), .sel(comparator_1_lt));
  Multiplexer #(.enable("false")) multiplexer_4 (
    .in0(in_4[1]), .in1(in_2[1]), .out(multiplexer_4_out), .sel(comparator_1_lt));
  Multiplexer #(.enable("false")) multiplexer_5 (
    .in0(in_2[2]), .in1(in_4[2]), .out(multiplexer_5_out), .sel(comparator_1_lt));
  Multiplexer #(.enable("false")) multiplexer_6 (
    .in0(in_4[2]), .in1(in_2[2]), .out(multiplexer_6_out), .sel(comparator_1_lt));
  Multiplexer #(.enable("false")) multiplexer_7 (
    .in0(in_2[3]), .in1(in_4[3]), .out(multiplexer_7_out), .sel(comparator_1_lt));
  Multiplexer #(.enable("false")) multiplexer_8 (
    .in0(in_4[3]), .in1(in_2[3]), .out(multiplexer_8_out), .sel(comparator_1_lt));
  and and_1 (and_1_out, not_1_out, in_1);
  and and_2 (and_2_out, in_1, in_3, comparator_1_gt);
  and and_3 (and_3_out, comparator_1_lt, not_2_out, not_3_out);
  xor xor_1 (xor_1_out, in_1, in_3);
  not not_4 (not_4_out, xor_1_out);
  Subtractor #(.width(1)) subtractor_1 (
    .a(multiplexer_1_out), .b(multiplexer_2_out), .out(subtractor_1_out), .bout(subtractor_1_bout));  // open: bin
  Subtractor #(.width(1)) subtractor_2 (
    .a(multiplexer_3_out), .b(multiplexer_4_out), .out(subtractor_2_out), .bin(subtractor_1_bout),
    .bout(subtractor_2_bout));
  Subtractor #(.width(1)) subtractor_3 (
    .a(multiplexer_5_out), .b(multiplexer_6_out), .out(subtractor_3_out), .bin(subtractor_2_bout),
    .bout(subtractor_3_bout));
  Subtractor #(.width(1)) subtractor_4 (
    .a(multiplexer_7_out), .b(multiplexer_8_out), .out(subtractor_4_out), .bin(subtractor_3_bout));  // open: bout
  or or_1 (out_5, and_1_out, and_2_out, and_3_out);
  _7_Segment_Display u_7_segment_display_1 (.g(out_5));  // open: f, a, b, e, d, c, dp
  and and_4 (and_4_out[0], xor_1_out, adder_1_out);
  and and_5 (and_4_out[1], xor_1_out, adder_2_out);
  and and_6 (and_4_out[2], xor_1_out, adder_3_out);
  and and_7 (and_4_out[3], xor_1_out, adder_4_out);
  and and_8 (and_8_out[0], not_4_out, subtractor_1_out);
  and and_9 (and_8_out[1], not_4_out, subtractor_2_out);
  and and_10 (and_8_out[2], not_4_out, subtractor_3_out);
  and and_11 (and_8_out[3], not_4_out, subtractor_4_out);
  Hex_Digit_Display hex_digit_display_3 (.value(out_6));  // open: dp
  Multiplexer #(.width(4), .enable("false")) multiplexer_9 (
    .in0(and_8_out), .in1(and_4_out), .out(out_6), .sel(xor_1_out));
endmodule

module \_4位原码加法器  (
  input  in_1,
  input  [3:0] in_2,
  input  in_3,
  input  [3:0] in_4,
  output out_5,
  output [3:0] out_6
);

  wire adder_1_cout, adder_1_out, adder_2_cout, adder_2_out, adder_3_cout, adder_3_out, adder_4_out,
       and_1_out, and_2_out, and_3_out, comparator_1_gt, comparator_1_lt, multiplexer_1_out,
       multiplexer_2_out, multiplexer_3_out, multiplexer_4_out, multiplexer_5_out, multiplexer_6_out,
       multiplexer_7_out, multiplexer_8_out, not_1_out, subtractor_1_bout, subtractor_1_out,
       subtractor_2_bout, subtractor_2_out, subtractor_3_bout, subtractor_3_out, subtractor_4_out, xnor_1_out;
  wire [3:0] and_4_out, and_8_out;

  Hex_Digit_Display hex_digit_display_1 (.value(in_2));  // open: dp
  Hex_Digit_Display hex_digit_display_2 (.value(in_4));  // open: dp
  Comparator #(.width(4), .mode("unsigned")) comparator_1 (
    .a(in_2), .b(in_4), .gt(comparator_1_gt), .lt(comparator_1_lt));  // open: eq
  Adder #(.width(1)) adder_1 (.a(in_2[0]), .b(in_4[0]), .out(adder_1_out), .cin(1'b0), .cout(adder_1_cout));
  Adder #(.width(1)) adder_2 (.a(in_2[1]), .b(in_4[1]), .out(adder_2_out), .cin(adder_1_cout), .cout(adder_2_cout));
  Adder #(.width(1)) adder_3 (.a(in_2[2]), .b(in_4[2]), .out(adder_3_out), .cin(adder_2_cout), .cout(adder_3_cout));
  Adder #(.width(1)) adder_4 (.a(in_2[3]), .b(in_4[3]), .out(adder_4_out), .cin(adder_3_cout));  // open: cout
  Multiplexer #(.enable("false")) multiplexer_1 (
    .in0(in_2[0]), .in1(in_4[0]), .out(multiplexer_1_out), .sel(comparator_1_lt));
  Multiplexer #(.enable("false")) multiplexer_2 (
    .in0(in_4[0]), .in1(in_2[0]), .out(multiplexer_2_out), .sel(comparator_1_lt));
  Multiplexer #(.enable("false")) multiplexer_3 (
    .in0(in_2[1]), .in1(in_4[1]), .out(multiplexer_3_out), .sel(comparator_1_lt));
  Multiplexer #(.enable("false")) multiplexer_4 (
    .in0(in_4[1]), .in1(in_2[1]), .out(multiplexer_4_out), .sel(comparator_1_lt));
  Multiplexer #(.enable("false")) multiplexer_5 (
    .in0(in_2[2]), .in1(in_4[2]), .out(multiplexer_5_out), .sel(comparator_1_lt));
  Multiplexer #(.enable("false")) multiplexer_6 (
    .in0(in_4[2]), .in1(in_2[2]), .out(multiplexer_6_out), .sel(comparator_1_lt));
  Multiplexer #(.enable("false")) multiplexer_7 (
    .in0(in_2[3]), .in1(in_4[3]), .out(multiplexer_7_out), .sel(comparator_1_lt));
  Multiplexer #(.enable("false")) multiplexer_8 (
    .in0(in_4[3]), .in1(in_2[3]), .out(multiplexer_8_out), .sel(comparator_1_lt));
  and and_1 (and_1_out, in_3, in_1);
  and and_2 (and_2_out, in_1, comparator_1_gt);
  and and_3 (and_3_out, comparator_1_lt, in_3);
  xnor xnor_1 (xnor_1_out, in_1, in_3);
  not not_1 (not_1_out, xnor_1_out);
  Subtractor #(.width(1)) subtractor_1 (
    .a(multiplexer_1_out), .b(multiplexer_2_out), .out(subtractor_1_out), .bout(subtractor_1_bout));  // open: bin
  Subtractor #(.width(1)) subtractor_2 (
    .a(multiplexer_3_out), .b(multiplexer_4_out), .out(subtractor_2_out), .bin(subtractor_1_bout),
    .bout(subtractor_2_bout));
  Subtractor #(.width(1)) subtractor_3 (
    .a(multiplexer_5_out), .b(multiplexer_6_out), .out(subtractor_3_out), .bin(subtractor_2_bout),
    .bout(subtractor_3_bout));
  Subtractor #(.width(1)) subtractor_4 (
    .a(multiplexer_7_out), .b(multiplexer_8_out), .out(subtractor_4_out), .bin(subtractor_3_bout));  // open: bout
  or or_1 (out_5, and_1_out, and_2_out, and_3_out);
  _7_Segment_Display u_7_segment_display_1 (.g(out_5));  // open: f, a, b, e, d, c, dp
  and and_4 (and_4_out[0], xnor_1_out, adder_1_out);
  and and_5 (and_4_out[1], xnor_1_out, adder_2_out);
  and and_6 (and_4_out[2], xnor_1_out, adder_3_out);
  and and_7 (and_4_out[3], xnor_1_out, adder_4_out);
  and and_8 (and_8_out[0], not_1_out, subtractor_1_out);
  and and_9 (and_8_out[1], not_1_out, subtractor_2_out);
  and and_10 (and_8_out[2], not_1_out, subtractor_3_out);
  and and_11 (and_8_out[3], not_1_out, subtractor_4_out);
  Hex_Digit_Display hex_digit_display_3 (.value(out_6));  // open: dp
  Multiplexer #(.width(4), .enable("false")) multiplexer_9 (
    .in0(and_8_out), .in1(and_4_out), .out(out_6), .sel(xnor_1_out));
endmodule

module \_4位反码加法器  (
  input  in_1,
  input  [3:0] in_2,
  input  in_3,
  input  [3:0] in_4
);

  wire and_1_out, and_2_out, multiplexer_11_out, multiplexer_12_out, \n4位原码加法器_1_out_5 , not_1_out,
       not_2_out, not_3_out, not_4_out, not_5_out, not_6_out, not_7_out, not_8_out, not_9_out, not_10_out;
  wire [3:0] multiplexer_1_out, multiplexer_2_out, multiplexer_6_out, multiplexer_7_out, multiplexer_13_out,
       multiplexer_14_out, \n4位原码加法器_1_out_6 ;

  _7_Segment_Display u_7_segment_display_1 (.g(multiplexer_11_out));  // open: f, a, b, e, d, c, dp
  Hex_Digit_Display hex_digit_display_1 (.value(multiplexer_1_out));  // open: dp
  _7_Segment_Display u_7_segment_display_2 (.g(multiplexer_12_out));  // open: f, a, b, e, d, c, dp
  Hex_Digit_Display hex_digit_display_2 (.value(multiplexer_6_out));  // open: dp
  not not_1 (not_1_out, in_2[0]);
  not not_2 (not_2_out, in_2[1]);
  not not_3 (not_3_out, in_2[2]);
  not not_4 (not_4_out, in_2[3]);
  not not_5 (not_5_out, in_4[0]);
  not not_6 (not_6_out, in_4[1]);
  not not_7 (not_7_out, in_4[2]);
  not not_8 (not_8_out, in_4[3]);
  Multiplexer #(.width(4), .enable("false")) multiplexer_1 (
    .in0(in_2), .in1(multiplexer_13_out), .out(multiplexer_1_out), .sel(in_1));
  Multiplexer #(.enable("false")) multiplexer_2 (
    .in0(in_2[0]), .in1(not_1_out), .out(multiplexer_2_out[0]), .sel(in_1));
  Multiplexer #(.enable("false")) multiplexer_3 (
    .in0(in_2[1]), .in1(not_2_out), .out(multiplexer_2_out[1]), .sel(in_1));
  Multiplexer #(.enable("false")) multiplexer_4 (
    .in0(in_2[2]), .in1(not_3_out), .out(multiplexer_2_out[2]), .sel(in_1));
  Multiplexer #(.enable("false")) multiplexer_5 (
    .in0(in_2[3]), .in1(not_4_out), .out(multiplexer_2_out[3]), .sel(in_1));
  Multiplexer #(.width(4), .enable("false")) multiplexer_6 (
    .in0(in_4), .in1(multiplexer_14_out), .out(multiplexer_6_out), .sel(in_3));
  Multiplexer #(.enable("false")) multiplexer_7 (
    .in0(in_4[0]), .in1(not_5_out), .out(multiplexer_7_out[0]), .sel(in_3));
  Multiplexer #(.enable("false")) multiplexer_8 (
    .in0(in_4[1]), .in1(not_6_out), .out(multiplexer_7_out[1]), .sel(in_3));
  Multiplexer #(.enable("false")) multiplexer_9 (
    .in0(in_4[2]), .in1(not_7_out), .out(multiplexer_7_out[2]), .sel(in_3));
  Multiplexer #(.enable("false")) multiplexer_10 (
    .in0(in_4[3]), .in1(not_8_out), .out(multiplexer_7_out[3]), .sel(in_3));
  and and_1 (and_1_out, in_1, not_1_out, not_2_out, not_3_out, not_4_out);
  and and_2 (and_2_out, in_3, not_5_out, not_6_out, not_7_out, not_8_out);
  Multiplexer #(.enable("false")) multiplexer_11 (
    .in0(in_1), .in1(not_9_out), .out(multiplexer_11_out), .sel(and_1_out));
  not not_9 (not_9_out, in_1);
  Multiplexer #(.enable("false")) multiplexer_12 (
    .in0(in_3), .in1(not_10_out), .out(multiplexer_12_out), .sel(and_2_out));
  not not_10 (not_10_out, in_3);
  Multiplexer #(.width(4), .enable("false")) multiplexer_13 (
    .in0(multiplexer_2_out), .in1(in_2), .out(multiplexer_13_out), .sel(and_1_out));
  Multiplexer #(.width(4), .enable("false")) multiplexer_14 (
    .in0(multiplexer_7_out), .in1(in_4), .out(multiplexer_14_out), .sel(and_2_out));
  \_4位原码加法器  \u_4位原码加法器_1  (
    .in_1(multiplexer_11_out), .in_2(multiplexer_13_out), .in_3(multiplexer_12_out),
    .in_4(multiplexer_14_out), .out_5(\n4位原码加法器_1_out_5 ), .out_6(\n4位原码加法器_1_out_6 ));
  _7_Segment_Display u_7_segment_display_3 (.g(\n4位原码加法器_1_out_5 ));  // open: f, a, b, e, d, c, dp
  Hex_Digit_Display hex_digit_display_3 (.value(\n4位原码加法器_1_out_6 ));  // open: dp
endmodule
